// Logisim project proj_3.circ as structural Verilog: 4 circuits, main circuit main
module main (
  input  x
);

  _7_Segment_Display u_7_segment_display_1 ();  // open: g, f, a, b, e, d, c, dp
  _7_Segment_Display u_7_segment_display_2 ();  // open: g, f, a, b, e, d, c, dp
endmodule

module base_10_up_down_counter (
);

  wire clock_1_out, j_k_ff_1_q, j_k_ff_1_qn, j_k_ff_2_q, j_k_ff_2_qn, j_k_ff_3_q, j_k_ff_3_qn, j_k_ff_4_qn;

  Clock clock_1 (.out(clock_1_out));
  J_K_Flip_Flop j_k_ff_1 (
    .J(1'b1), .clk(clock_1_out), .K(1'b1), .Q(j_k_ff_1_q), .Qn(j_k_ff_1_qn));  // open: preset, en, reset
  J_K_Flip_Flop j_k_ff_2 (
    .J(1'b1), .clk(j_k_ff_1_q), .K(1'b1), .Q(j_k_ff_2_q), .Qn(j_k_ff_2_qn));  // open: preset, en, reset
  J_K_Flip_Flop j_k_ff_3 (
    .J(1'b1), .clk(j_k_ff_2_q), .K(1'b1), .Q(j_k_ff_3_q), .Qn(j_k_ff_3_qn));  // open: preset, en, reset
  J_K_Flip_Flop j_k_ff_4 (.J(1'b1), .clk(j_k_ff_3_q), .K(1'b1), .Qn(j_k_ff_4_qn));  // open: Q, preset, en, reset
  // Probe on j_k_ff_4_qn
  // Probe on j_k_ff_3_qn
  // Probe on j_k_ff_2_qn
  // Probe on j_k_ff_1_qn
endmodule

module base_6_up_down_counter (
  input  in_1,
  input  in_2,
  input  in_3,
  input  x
);

  wire and_1_out, clock_1_out;

  Clock clock_1 (.out(clock_1_out));
  J_K_Flip_Flop j_k_ff_1 (.J(x), .clk(clock_1_out), .K(x), .Q(in_1));  // open: Qn, preset, en, reset
  J_K_Flip_Flop j_k_ff_2 (.J(in_1), .clk(clock_1_out), .K(in_1), .Q(in_2));  // open: Qn, preset, en, reset
  and and_1 (and_1_out, in_1, in_2);
  J_K_Flip_Flop j_k_ff_3 (.J(and_1_out), .clk(clock_1_out), .K(and_1_out), .Q(in_3));  // open: Qn, preset, en, reset
endmodule

module base_6_up_down_counter2 (
  output out_1,
  output out_2,
  output out_3
);

  wire and_1_out, clock_1_out;

  Clock clock_1 (.out(clock_1_out));
  T_Flip_Flop t_ff_1 (.clk(clock_1_out), .T(1'b1), .Q(out_3));  // open: Qn, preset, reset, en
  T_Flip_Flop t_ff_2 (.clk(clock_1_out), .T(out_3), .Q(out_2));  // open: Qn, preset, reset, en
  and and_1 (and_1_out, out_2, out_3);
  T_Flip_Flop t_ff_3 (.clk(clock_1_out), .T(and_1_out), .Q(out_1));  // open: Qn, preset, reset, en
endmodule
